// Logisim project 8-8 bit_ReadFile .circ as structural Verilog: 1 circuit, main circuit main
module main (
  input  [2:0] ReadReg1,
  input  [2:0] ReadReg2,
  input  [7:0] WriteData,
  input  WritePin,
  output [7:0] OutputData1,
  output [7:0] OutputData2
);

  wire Clk_out, undriven;
  wire [7:0] register_1_q, register_2_q, register_3_q, register_4_q, register_5_q, register_6_q,
       register_7_q, register_8_q;

  Clock Clk (.out(Clk_out));
  Register register_1 (.Q(register_1_q));  // open: D, en, clk, clr
  Register register_2 (.Q(register_2_q));  // open: D, en, clk, clr
  Register register_3 (.Q(register_3_q));  // open: D, en, clk, clr
  Register register_4 (.D(WriteData), .en(WritePin), .Q(register_4_q), .clk(Clk_out));  // open: clr
  Register register_5 (.Q(register_5_q));  // open: D, en, clk, clr
  Register register_6 (.Q(register_6_q));  // open: D, en, clk, clr
  Register register_7 (.Q(register_7_q), .clk(undriven));  // open: D, en, clr
  Register register_8 (.Q(register_8_q));  // open: D, en, clk, clr
  Multiplexer #(.select(3), .width(8), .enable("false")) multiplexer_1 (
    .in0(register_1_q), .in1(register_2_q), .in2(register_3_q), .in3(register_4_q), .in4(register_5_q),
    .in5(register_6_q), .in6(register_7_q), .in7(register_8_q), .out(OutputData1), .sel(ReadReg1));
  Multiplexer #(.select(3), .width(8), .enable("false")) multiplexer_2 (
    .in0(register_1_q), .in1(register_2_q), .in2(register_3_q), .in3(register_4_q), .in4(register_5_q),
    .in5(register_6_q), .in6(register_7_q), .in7(register_8_q), .out(OutputData2), .sel(ReadReg2));
endmodule
