// Logisim project 8-8 bit_WriteFile.circ as structural Verilog: 1 circuit, main circuit main
module main (
  input  WritePin,
  input  [7:0] WriteData,
  input  [2:0] WriteReg,
  output [7:0] OutputData_at_3rd
);

  wire and_1_out, and_2_out, and_3_out, and_4_out, and_5_out, and_6_out, and_7_out, and_8_out, Clk_out,
       decoder_1_out0, decoder_1_out1, decoder_1_out2, decoder_1_out3, decoder_1_out4, decoder_1_out5,
       decoder_1_out6, decoder_1_out7;

  Clock Clk (.out(Clk_out));
  Decoder #(.select(3), .enable("false")) decoder_1 (
    .out0(decoder_1_out0), .out1(decoder_1_out1), .out2(decoder_1_out2), .out3(decoder_1_out3),
    .out4(decoder_1_out4), .out5(decoder_1_out5), .out6(decoder_1_out6), .out7(decoder_1_out7), .sel(WriteReg));
  and and_1 (and_1_out, WritePin, decoder_1_out0);
  and and_2 (and_2_out, WritePin, decoder_1_out1);
  and and_3 (and_3_out, WritePin, decoder_1_out2);
  and and_4 (and_4_out, WritePin, decoder_1_out3);
  and and_5 (and_5_out, WritePin, decoder_1_out4);
  and and_6 (and_6_out, WritePin, decoder_1_out5);
  and and_7 (and_7_out, WritePin, decoder_1_out6);
  and and_8 (and_8_out, WritePin, decoder_1_out7);
  Register register_1 (.D(WriteData), .en(and_1_out), .clk(Clk_out));  // open: Q, clr
  Register register_2 (.D(WriteData), .en(and_2_out), .clk(Clk_out));  // open: Q, clr
  Register register_3 (.D(WriteData), .en(and_3_out), .Q(OutputData_at_3rd), .clk(Clk_out));  // open: clr
  Register register_4 (.D(WriteData), .en(and_4_out), .clk(Clk_out));  // open: Q, clr
  Register register_5 (.D(WriteData), .en(and_5_out), .clk(Clk_out));  // open: Q, clr
  Register register_6 (.D(WriteData), .en(and_6_out), .clk(Clk_out));  // open: Q, clr
  Register register_7 (.D(WriteData), .en(and_7_out), .clk(Clk_out));  // open: Q, clr
  Register register_8 (.D(WriteData), .en(and_8_out), .clk(Clk_out));  // open: Q, clr
endmodule
