// Logisim project MIPsRegisterFile.circ as structural Verilog: 1 circuit, main circuit main
module main (
  input  [4:0] ReadReg1,
  input  [4:0] ReadReg2,
  input  Write,
  input  Clk,
  input  [31:0] WriteData,
  input  [4:0] WriteReg,
  output [31:0] OutputData1,
  output [31:0] OutputData2
);

  wire and_1_out, and_2_out, and_3_out, and_4_out, and_5_out, and_6_out, and_7_out, and_8_out, and_9_out,
       and_10_out, and_11_out, and_12_out, and_13_out, and_14_out, and_15_out, and_16_out, and_17_out,
       and_18_out, and_19_out, and_20_out, and_21_out, and_22_out, and_23_out, and_24_out, and_25_out,
       and_26_out, and_27_out, and_28_out, and_29_out, and_30_out, and_31_out, and_32_out, decoder_1_out0,
       decoder_1_out1, decoder_1_out2, decoder_1_out3, decoder_1_out4, decoder_1_out5, decoder_1_out6,
       decoder_1_out7, decoder_1_out8, decoder_1_out9, decoder_1_out10, decoder_1_out11, decoder_1_out12,
       decoder_1_out13, decoder_1_out14, decoder_1_out15, decoder_1_out16, decoder_1_out17, decoder_1_out18,
       decoder_1_out19, decoder_1_out20, decoder_1_out21, decoder_1_out22, decoder_1_out23, decoder_1_out24,
       decoder_1_out25, decoder_1_out26, decoder_1_out27, decoder_1_out28, decoder_1_out29, decoder_1_out30,
       decoder_1_out31;
  wire [31:0] s0_q, s1_q, s2_q, s3_q, s4_q, s5_q, s6_q, s7_q, s8_q, s9_q, s10_q, s11_q, s12_q, s13_q, s14_q,
       s15_q, s16_q, s17_q, s18_q, s19_q, s20_q, s21_q, s22_q, s23_q, s24_q, s25_q, s26_q, s27_q, s28_q,
       s29_q, s30_q, s31_q;

  Decoder #(.select(5), .enable("false")) decoder_1 (
    .out0(decoder_1_out0), .out1(decoder_1_out1), .out2(decoder_1_out2), .out3(decoder_1_out3),
    .out4(decoder_1_out4), .out5(decoder_1_out5), .out6(decoder_1_out6), .out7(decoder_1_out7),
    .out8(decoder_1_out8), .out9(decoder_1_out9), .out10(decoder_1_out10), .out11(decoder_1_out11),
    .out12(decoder_1_out12), .out13(decoder_1_out13), .out14(decoder_1_out14), .out15(decoder_1_out15),
    .out16(decoder_1_out16), .out17(decoder_1_out17), .out18(decoder_1_out18), .out19(decoder_1_out19),
    .out20(decoder_1_out20), .out21(decoder_1_out21), .out22(decoder_1_out22), .out23(decoder_1_out23),
    .out24(decoder_1_out24), .out25(decoder_1_out25), .out26(decoder_1_out26), .out27(decoder_1_out27),
    .out28(decoder_1_out28), .out29(decoder_1_out29), .out30(decoder_1_out30), .out31(decoder_1_out31),
    .sel(WriteReg));
  and and_1 (and_1_out, Write, decoder_1_out18);
  and and_2 (and_2_out, Write, decoder_1_out19);
  and and_3 (and_3_out, Write, decoder_1_out0);
  and and_4 (and_4_out, Write, decoder_1_out1);
  and and_5 (and_5_out, Write, decoder_1_out2);
  and and_6 (and_6_out, Write, decoder_1_out3);
  and and_7 (and_7_out, Write, decoder_1_out4);
  and and_8 (and_8_out, Write, decoder_1_out5);
  and and_9 (and_9_out, Write, decoder_1_out6);
  and and_10 (and_10_out, Write, decoder_1_out7);
  and and_11 (and_11_out, Write, decoder_1_out8);
  and and_12 (and_12_out, Write, decoder_1_out9);
  and and_13 (and_13_out, Write, decoder_1_out10);
  and and_14 (and_14_out, Write, decoder_1_out11);
  and and_15 (and_15_out, Write, decoder_1_out12);
  and and_16 (and_16_out, Write, decoder_1_out13);
  and and_17 (and_17_out, Write, decoder_1_out14);
  and and_18 (and_18_out, Write, decoder_1_out15);
  and and_19 (and_19_out, Write, decoder_1_out16);
  and and_20 (and_20_out, Write, decoder_1_out17);
  Register #(.width(32)) s18 (.D(WriteData), .en(and_1_out), .Q(s18_q), .clk(Clk));  // open: clr
  Register #(.width(32)) s19 (.D(WriteData), .en(and_2_out), .Q(s19_q), .clk(Clk));  // open: clr
  and and_21 (and_21_out, Write, decoder_1_out20);
  and and_22 (and_22_out, Write, decoder_1_out21);
  and and_23 (and_23_out, Write, decoder_1_out22);
  and and_24 (and_24_out, Write, decoder_1_out23);
  and and_25 (and_25_out, Write, decoder_1_out24);
  and and_26 (and_26_out, Write, decoder_1_out25);
  and and_27 (and_27_out, Write, decoder_1_out26);
  and and_28 (and_28_out, Write, decoder_1_out27);
  and and_29 (and_29_out, Write, decoder_1_out28);
  and and_30 (and_30_out, Write, decoder_1_out29);
  and and_31 (and_31_out, Write, decoder_1_out30);
  and and_32 (and_32_out, Write, decoder_1_out31);
  Register #(.width(32)) s0 (.D(WriteData), .en(and_3_out), .Q(s0_q), .clk(Clk));  // open: clr
  Register #(.width(32)) s1 (.D(WriteData), .en(and_4_out), .Q(s1_q), .clk(Clk));  // open: clr
  Register #(.width(32)) s2 (.D(WriteData), .en(and_5_out), .Q(s2_q), .clk(Clk));  // open: clr
  Register #(.width(32)) s3 (.D(WriteData), .en(and_6_out), .Q(s3_q), .clk(Clk));  // open: clr
  Register #(.width(32)) s4 (.D(WriteData), .en(and_7_out), .Q(s4_q), .clk(Clk));  // open: clr
  Register #(.width(32)) s5 (.D(WriteData), .en(and_8_out), .Q(s5_q), .clk(Clk));  // open: clr
  Register #(.width(32)) s6 (.D(WriteData), .en(and_9_out), .Q(s6_q), .clk(Clk));  // open: clr
  Register #(.width(32)) s7 (.D(WriteData), .en(and_10_out), .Q(s7_q), .clk(Clk));  // open: clr
  Register #(.width(32)) s8 (.D(WriteData), .en(and_11_out), .Q(s8_q), .clk(Clk));  // open: clr
  Register #(.width(32)) s9 (.D(WriteData), .en(and_12_out), .Q(s9_q), .clk(Clk));  // open: clr
  Register #(.width(32)) s10 (.D(WriteData), .en(and_13_out), .Q(s10_q), .clk(Clk));  // open: clr
  Register #(.width(32)) s11 (.D(WriteData), .en(and_14_out), .Q(s11_q), .clk(Clk));  // open: clr
  Register #(.width(32)) s12 (.D(WriteData), .en(and_15_out), .Q(s12_q), .clk(Clk));  // open: clr
  Register #(.width(32)) s13 (.D(WriteData), .en(and_16_out), .Q(s13_q), .clk(Clk));  // open: clr
  Register #(.width(32)) s14 (.D(WriteData), .en(and_17_out), .Q(s14_q), .clk(Clk));  // open: clr
  Register #(.width(32)) s15 (.D(WriteData), .en(and_18_out), .Q(s15_q), .clk(Clk));  // open: clr
  Register #(.width(32)) s16 (.D(WriteData), .en(and_19_out), .Q(s16_q), .clk(Clk));  // open: clr
  Register #(.width(32)) s17 (.D(WriteData), .en(and_20_out), .Q(s17_q), .clk(Clk));  // open: clr
  Register #(.width(32)) s20 (.D(WriteData), .en(and_21_out), .Q(s20_q), .clk(Clk));  // open: clr
  Register #(.width(32)) s21 (.D(WriteData), .en(and_22_out), .Q(s21_q), .clk(Clk));  // open: clr
  Register #(.width(32)) s22 (.D(WriteData), .en(and_23_out), .Q(s22_q), .clk(Clk));  // open: clr
  Register #(.width(32)) s23 (.D(WriteData), .en(and_24_out), .Q(s23_q), .clk(Clk));  // open: clr
  Register #(.width(32)) s24 (.D(WriteData), .en(and_25_out), .Q(s24_q), .clk(Clk));  // open: clr
  Register #(.width(32)) s25 (.D(WriteData), .en(and_26_out), .Q(s25_q), .clk(Clk));  // open: clr
  Register #(.width(32)) s26 (.D(WriteData), .en(and_27_out), .Q(s26_q), .clk(Clk));  // open: clr
  Register #(.width(32)) s27 (.D(WriteData), .en(and_28_out), .Q(s27_q), .clk(Clk));  // open: clr
  Register #(.width(32)) s28 (.D(WriteData), .en(and_29_out), .Q(s28_q), .clk(Clk));  // open: clr
  Register #(.width(32)) s29 (.D(WriteData), .en(and_30_out), .Q(s29_q), .clk(Clk));  // open: clr
  Register #(.width(32)) s30 (.D(WriteData), .en(and_31_out), .Q(s30_q), .clk(Clk));  // open: clr
  Register #(.width(32)) s31 (.D(WriteData), .en(and_32_out), .Q(s31_q), .clk(Clk));  // open: clr
  Multiplexer #(.select(5), .width(32), .enable("false")) multiplexer_1 (
    .in0(s0_q), .in1(s1_q), .in2(s2_q), .in3(s3_q), .in4(s4_q), .in5(s5_q), .in6(s6_q), .in7(s7_q),
    .in8(s8_q), .in9(s9_q), .in10(s10_q), .in11(s11_q), .in12(s12_q), .in13(s13_q), .in14(s14_q),
    .in15(s15_q), .in16(s16_q), .in17(s17_q), .in18(s18_q), .in19(s19_q), .in20(s20_q), .in21(s21_q),
    .in22(s22_q), .in23(s23_q), .in24(s24_q), .in25(s25_q), .in26(s26_q), .in27(s27_q), .in28(s28_q),
    .in29(s29_q), .in30(s30_q), .in31(s31_q), .out(OutputData1), .sel(ReadReg1));
  Multiplexer #(.select(5), .width(32)) multiplexer_2 (
    .in0(s0_q), .in1(s1_q), .in2(s2_q), .in3(s3_q), .in4(s4_q), .in5(s5_q), .in6(s6_q), .in7(s7_q),
    .in8(s8_q), .in9(s9_q), .in10(s10_q), .in11(s11_q), .in12(s12_q), .in13(s13_q), .in14(s14_q),
    .in15(s15_q), .in16(s16_q), .in17(s17_q), .in18(s18_q), .in19(s19_q), .in20(s20_q), .in21(s21_q),
    .in22(s22_q), .in23(s23_q), .in24(s24_q), .in25(s25_q), .in26(s26_q), .in27(s27_q), .in28(s28_q),
    .in29(s29_q), .in30(s30_q), .in31(s31_q), .out(OutputData2), .sel(ReadReg2));  // open: en
endmodule
